# Fritzing sketch PowerGuard (saved by Fritzing 0.9.10b)
breadboards: 1

parts:
  MH-ET_LIVE_ESP32_DEVKIT1 = MH-ET LIVE ESP32 DEVKIT 38 pins
  U2 = mystery part, 3 pins [chip_label=DS18B20 part_number=DS18B20]
  LED3 = LED - 5mm [color="Green (565nm)" current=0.030 package="5 mm [THT]"]
  LED4 = LED - 5mm [color="Red (633nm)" current=0.030 package="5 mm [THT]"]
  R5 = Resistor [tolerance=±5% power=0.25 resistance=220 package=THT]
  R6 = Resistor [tolerance=±5% power=0.25 resistance=330 package=THT]
  U3 = mystery part, 3 pins [chip_label=DS18B20 part_number=DS18B20]
  M1 = AC-05-03
  R4 = Resistor [tolerance=±5% power=0.25 resistance=4.7k package=THT]
  Bauteil2 = I2C level shifter bidirectional
  J4 = female pin header, 6 pins [form="♀ (female)"]
  LED5 = LED - 5mm [color="Yellow (592nm)" current=0.030 package="5 mm [THT]"]
  R7 = Resistor [tolerance=±5% power=0.25 resistance=220 package=THT]

nets:
  N1: MH-ET_LIVE_ESP32_DEVKIT1.3V3, U2.pin3, U3.pin3, R4.Pin_1, Bauteil2.LV
  N2: MH-ET_LIVE_ESP32_DEVKIT1.IO25, U2.pin2, U3.pin2, R4.Pin_0
  N3: MH-ET_LIVE_ESP32_DEVKIT1.5V, M1.pin_3, Bauteil2.HV, J4.pin6
  N4: MH-ET_LIVE_ESP32_DEVKIT1.GND#64, U2.pin1, LED3.cathode, LED4.cathode, U3.pin1, M1.pin_4, Bauteil2.GND, J4.pin5, R7.Pin_0
  N5: MH-ET_LIVE_ESP32_DEVKIT1.IO23, R5.Pin_0
  N6: MH-ET_LIVE_ESP32_DEVKIT1.IO22, LED5.cathode
  N7: MH-ET_LIVE_ESP32_DEVKIT1.IO19, R6.Pin_0
  N8: MH-ET_LIVE_ESP32_DEVKIT1.IO18, Bauteil2.LV1
  N9: MH-ET_LIVE_ESP32_DEVKIT1.IO17, Bauteil2.LV2
  N10: LED3.anode, R6.Pin_1
  N11: LED4.anode, R5.Pin_1
  N12: Bauteil2.HV1, J4.pin2
  N13: Bauteil2.HV2, J4.pin3
  N14: LED5.anode, R7.Pin_1

notes:
  Schaltkanäle über Relais
  (CHN2|CHN1|DC-|DC+) (5V)
  Spannungsversorgung über AC-05-03 oder über Wächterplatine
  2 Relais
  CHN1 -> 5V
  CHN2 -> 12V (LED-Treibernetzteil)
  (Versorgung LV und HV der Heizstabsteuerung)
  Aufgabe: Überwachung der Max-Temperatur + bei Störungen bzw. Limitüberschreitung der Heizstabsteuerung die Enegrie entziehen.

custom parts:
  MH-ET LIVE ESP32 DEVKIT 38 pins: http://mh.nodebb.com/topic/2/mh-et-live-esp32-devkit
  AC-05-03: AC-DC 220V to 5V Step-Down Power Supply Module
